# Fritzing sketch LM35DZ (saved by Fritzing 0.9.2b)
breadboards: 1

parts:
  T1 = LM35 Temperature Sensor [thermistor_type=NTC package="TO92 [THT]"]
  Raspberry_Pi1 = Raspberry Pi 2
  IC1 = IC, DIP package, 8 pins [chip_label=MCP3002]

nets (from the schematic view):
  N1: T1.Vout, IC1.pin2
  GND: T1.GND, Raspberry_Pi1.GND, IC1.pin4
  3V3: Raspberry_Pi1.3v3, Raspberry_Pi1.3V3, IC1.pin8
  N2: Raspberry_Pi1.GPIO10, IC1.pin5
  N3: Raspberry_Pi1.GPIO9, IC1.pin6
  N4: Raspberry_Pi1.GPIO11, IC1.pin7
  N5: Raspberry_Pi1.GPIO8, IC1.pin1
